# Fritzing sketch Motors (saved by Fritzing 0.9.3b)
breadboards: 1

parts:
  Raspberry_Pi_1 = Raspberry Pi 3 [part_number=RPI-3-V1.2]
  PWM1 = PCA9685 16x12-bit PWM Breakout
  MOTOR1 = 28BYJ-48 Stepper Motor
  X1 = X113647 Stepper Driver Board [package=board]
  BAT1 = BC9VPC [package=bc9vpc]
  J1 = Basic Servo
  M1 = DC Motor
  BAT2 = BC9VPC [package=bc9vpc]
  BAT3 = BC9VPC [package=bc9vpc]
  S1 = H-Bridge with L298N
  M2 = DC Motor

nets:
  N1: Raspberry_Pi_1.3v3, PWM1.no_name_yet#505
  N2: Raspberry_Pi_1.GPIO2, PWM1.no_name_yet#504
  N3: Raspberry_Pi_1.GPIO3, PWM1.no_name_yet#503
  GND: Raspberry_Pi_1.GND, PWM1.no_name_yet#501, PWM1.no_name_yet#701, PWM1.no_name_yet#1000, X1.GND, BAT1.V-, BAT2.V-, BAT3.V-, S1.GND
  N4: Raspberry_Pi_1.GPIO17, S1.IN1
  N5: Raspberry_Pi_1.GPIO27, S1.IN2
  N6: Raspberry_Pi_1.GPIO6, X1.IN1
  N7: Raspberry_Pi_1.GPIO13, X1.IN2
  N8: Raspberry_Pi_1.GPIO19, X1.IN3
  N9: Raspberry_Pi_1.GPIO26, X1.IN4
  N10: Raspberry_Pi_1.GPIO24, S1.IN4
  N11: Raspberry_Pi_1.GPIO23, S1.IN3
  N12: PWM1.no_name_yet#0, J1.pulse
  N13: PWM1.no_name_yet#14, S1.ENB
  N14: PWM1.no_name_yet#15, S1.ENA
  N15: PWM1.no_name_yet#100, PWM1.no_name_yet#706, BAT3.V+
  N16: MOTOR1.BLUE, X1.BLUE
  N17: MOTOR1.PINK, X1.PINK
  N18: MOTOR1.RED, X1.YELLOW
  N19: MOTOR1.ORANGE, X1.ORANGE
  N20: MOTOR1.YELLOW, X1.RED
  N21: X1.+V, BAT1.V+
  N22: M1.pin_1, S1.M1-02
  N23: M1.pin_2, S1.M1-01
  N24: BAT2.V+, S1.12V
  N25: S1.M2-01, M2.pin_2
  N26: S1.M2-02, M2.pin_1

notes:
  Stepper Motor
  ULN2003 (IN1) = GPIO6
  ULN2003 (IN2) = GPIO13
  ULN2003 (IN3) = GPIO19
  ULN2003 (IN4) = GPIO26
  Servo Motor
  PCA9685 (SCL) = GPIO2 (SCL)
  PCA9685 (SDA) = GPIO3 (SDA)
  PCA9685 (VCC) = GPIO1 (3.3V)
  PCA9685 (0) = Motor
  DC Motor
  L298N (ENA) = PCA9685 (15 - PWM)
  L298N (IN1) = GPIO17
  L298N (IN2) = GPIO27
  L298N (ENB) = PCA9685 (14 - PWM)
  L298N (IN3) = GPIO23
  L298N (IN4) = GPIO24

custom parts:
  28BYJ-48 Stepper Motor: 28BYJ-48 gear-reduction stepper motor (small)
  X113647 Stepper Driver Board: A common stepper motor driver board based on ULN2003APG darlington array
  H-Bridge with L298N: h-bridge
