# Fritzing sketch proyecto 1 (saved by Fritzing 1.0.4)
breadboards: 1

parts:
  J1 = Basic Servo  # not connected
  Componente1 = HX711 Weighing Sensor Module  # not connected
  J2 = Piezo Speaker
  Componente2 = ADS1115
  R1 = Photocell (LDR) [power=0.25W dark_resistance_@0.01lx=300kΩ light_resistance_@100lx=400Ω luminance=10lx package=THT]  # not connected
  Componente3 = Adafruit SHT31-D [part_number="Adafruit #2857"]
  M1 = LJ12A3-4-Z [package=THT]  # not connected
  U2 = WS2812 RGB LED matrix 1x8  # not connected
  Load_Cell1 = Load Cell - Red/white/black/green  # not connected
  Componente4 = Adafruit PCA9685 PWM/Servo Breakout [part_number=815]
  U3 = WS2812 RGB LED matrix 1x8  # not connected
  MOTOR1 = 28BYJ-48 Stepper Motor  # not connected
  Componente5 = HX711 Weighing Sensor Module  # not connected
  Componente6 = HX711 Weighing Sensor Module  # not connected
  Componente7 = HX711 Weighing Sensor Module  # not connected
  BAT1 = BC9VPC [package=bc9vpc]
  X1 = X113647 Stepper Driver Board [package=board]
  VCC1 = 4 x AAA Battery Mount [internal_resistance=0.1Ω]
  CPU1 = NodeMCU WROOM ESP 32

nets:
  N1: J2.pin1, J2.pin2, Componente4.5.0V
  GND: Componente2.GND, Componente3.GND, VCC1.+
  N2: Componente2.SCL, Componente2.SDA, Componente3.SDA, Componente3.SCL, Componente4.SCL, CPU1.pin_5, CPU1.pin_6, CPU1.pin_7, CPU1.pin_8, CPU1.pin_9, CPU1.pin_24, CPU1.pin_25, CPU1.pin_26, CPU1.pin_27, CPU1.pin_28, CPU1.pin_29
  GND_2: Componente4.GND, BAT1.V+, X1.GND, VCC1.-
  N3: BAT1.V-, CPU1.pin_12, CPU1.pin_13, CPU1.pin_14, CPU1.pin_15, CPU1.pin_16
  N4: CPU1.pin_17, CPU1.pin_18, CPU1.pin_19, CPU1.pin_20, CPU1.pin_21

custom parts:
  ADS1115: ADC ADS1115
  Adafruit SHT31-D: Sensirion Temperature/Humidity sensors are some of the finest & highest-accuracy devices you can get. And, finally we have some that have a true I2C interface for easy reading. The SHT31-D sensor has an excellent ±2% relative humidity and ±0.3°C accuracy for most uses. We now use the version with a PTFE filter, it'll stay clean while still allowing humidity measurements to work Unlike earlier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
  LJ12A3-4-Z: LJ12A3-4-Z Proximity Sensor module.220V normally open.
  WS2812 RGB LED matrix 1x8: WS2812 matrix 1x8
  Load Cell - Red/white/black/green: A rectangle load cell/weighting pressure Sensor with four wires - Red, white, black, green. Normally corresponding with E+, E-, A+, A- respectively.
  Adafruit PCA9685 PWM/Servo Breakout: Using only two pins, control 16 free-running PWM outputs! I2C-controlled PWM driver with a built in clock. Unlike the TLC5940 family, you do not need to continuously send it signal tying up your microcontroller, its completely free running! 5V compliant, which means you can control it from a 3.3V microcontroller and still safely drive up to 6V outputs (this is good for when you want to control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
  28BYJ-48 Stepper Motor: 28BYJ-48 gear-reduction stepper motor (small)
  X113647 Stepper Driver Board: A common stepper motor driver board based on ULN2003APG darlington array
  NodeMCU WROOM ESP 32: 30 pol Development Kit
